// Logisim project ALU.circ as structural Verilog: 1 circuit, main circuit ALU
module ALU (
  input  [31:0] A,
  input  [31:0] B,
  input  [4:0] Shift,
  input  CarryIn,
  input  [3:0] Codop,
  input  [3:0] in_6,
  output [3:0] Flags,
  output [31:0] S
);

  wire CarryOutADC, CarryOutSBC, not_2_out, subtractor_1_bout;
  wire [31:0] not_1_out, PARM_ADC, PARM_AND, PARM_ASR, PARM_BIC, PARM_CMN, PARM_CMP, PARM_EOR, PARM_LSL,
       PARM_LSR, PARM_MUL, PARM_MVN, PARM_ORR, PARM_ROR, PARM_RSB, PARM_SBC, PARM_TST;

  assign not_1_out = ~A;  // NOT_Gate not_1, 32 bits wide
  assign PARM_AND = A & B;  // AND_Gate and_1, 32 bits wide
  assign PARM_EOR = A ^ B;  // XOR_Gate xor_1, 32 bits wide
  Shifter #(.width(32)) shifter_1 (.in(B), .\dist (Shift), .out(PARM_LSL));
  Shifter #(.shift("lr"), .width(32)) shifter_2 (.in(B), .\dist (Shift), .out(PARM_LSR));
  Shifter #(.shift("ar"), .width(32)) shifter_3 (.in(B), .\dist (Shift), .out(PARM_ASR));
  assign PARM_BIC = B & not_1_out;  // AND_Gate and_2, 32 bits wide
  Multiplexer #(.select(4), .width(32)) multiplexer_1 (
    .in0(PARM_AND), .in1(PARM_EOR), .in2(PARM_LSL), .in3(PARM_LSR), .in4(PARM_ASR), .in5(PARM_ADC),
    .in6(PARM_SBC), .in7(PARM_ROR), .in8(PARM_TST), .in9(PARM_RSB), .in10(PARM_CMP), .in11(PARM_CMN),
    .in12(PARM_ORR), .in13(PARM_MUL), .in14(PARM_BIC), .in15(PARM_MVN), .out({Flags[3], S[30:0]}), .sel(Codop));
  Comparator #(.width(32)) comparator_1 (.a({32{1'b0}}), .b({Flags[3], S[30:0]}), .eq(Flags[2]));  // open: gt, lt
  Adder #(.width(32)) adder_1 (.a(A), .b(B), .out(PARM_ADC), .cin(CarryIn), .cout(CarryOutADC));
  not not_2 (not_2_out, CarryIn);
  Subtractor #(.width(32)) subtractor_1 (.a(B), .b(A), .out(PARM_SBC), .bin(not_2_out), .bout(subtractor_1_bout));
  not not_3 (CarryOutSBC, subtractor_1_bout);
  Subtractor #(.width(32)) subtractor_2 (.a({32{1'b0}}), .b(A), .out(PARM_RSB));  // open: bin, bout
  assign PARM_MVN = ~A;  // NOT_Gate not_4, 32 bits wide
  Multiplexer #(.select(4)) multiplexer_2 (
    .in0(CarryOutADC), .in6(CarryOutSBC), .out(Flags[1]), .sel(in_6));  // open: in1, in2, in3, in4, in5, in7, in8, in9, in10, in11, in12, in13, in14, in15
  Shifter #(.shift("rr"), .width(32)) shifter_4 (.in(B), .\dist (Shift), .out(PARM_ROR));
  assign PARM_TST = A & B;  // AND_Gate and_3, 32 bits wide
  Subtractor #(.width(32)) subtractor_3 (.a(B), .b(A), .out(PARM_CMP));  // open: bin, bout
  Adder #(.width(32)) adder_2 (.a(A), .b(B), .out(PARM_CMN));  // open: cin, cout
  assign PARM_ORR = A | B;  // OR_Gate or_1, 32 bits wide
  Multiplier #(.width(32)) multiplier_1 (.a(A), .b(B), .out(PARM_MUL));  // open: cin, cout
  Pull_Resistor pull_resistor_1 (.node(Flags[1]));

  assign Flags[0] = 1'b0;
  assign S[31] = Flags[3];

  // Other names for the same wires on the sheet: C = Flags[1]; Z = Flags[2]; N = Flags[3]

  // Notes on the sheet:
  //   Note: for ROR, C = N
  //   Note 2: assume that shift > 0 for LSL and LSR
endmodule
