// Logisim project Ctl_Load_Store.circ as structural Verilog: 1 circuit, main circuit Load_Store
module Load_Store (
  input  Enable,
  input  [15:0] Instruction,
  input  Clk,
  input  Reset,
  input  [31:0] Stack_Pointer,
  output Store,
  output Load,
  output PC_Hold,
  output [2:0] Rmd,
  output [31:0] RAM_Addr
);

  wire and_1_out, and_2_out, not_1_out;
  wire [31:0] adder_1_out, bit_extender_1_out;

  and and_1 (and_1_out, not_1_out, Instruction[11]);
  not not_1 (not_1_out, PC_Hold);
  D_Flip_Flop d_ff_1 (.D(and_1_out), .clk(Clk), .Q(PC_Hold), .reset(Reset));  // open: Qn, preset
  assign bit_extender_1_out = {{24{Instruction[7]}}, Instruction[7:0]};  // Bit_Extender bit_extender_1
  Adder #(.width(32)) adder_1 (.a(bit_extender_1_out), .b(Stack_Pointer), .out(adder_1_out));  // open: cin, cout
  Multiplexer #(.width(3)) multiplexer_1 (.in0(3'b000), .in1(Instruction[10:8]), .out(Rmd), .sel(Enable));
  Multiplexer #(.width(32)) multiplexer_2 (.in0({32{1'b0}}), .in1(adder_1_out), .out(RAM_Addr), .sel(Enable));
  and and_2 (and_2_out, PC_Hold, Instruction[11]);
  Multiplexer multiplexer_3 (.in1(and_2_out), .out(PC_Hold), .sel(Enable));  // open: in0
  Multiplexer multiplexer_4 (.in0(1'b0), .in1(Instruction[11]), .out(Instruction[11]), .sel(Enable));
  Multiplexer multiplexer_5 (.in0(1'b0), .in1(Instruction[11]), .out(Instruction[11]), .sel(Enable));

  assign Load = Instruction[11];
  assign Store = Instruction[11];

  // Other names for the same wires on the sheet: Ram[7:0] = Instruction[7:0]; Rmd_t[2:0] = Instruction[10:8]

  // Notes on the sheet:
  //   Instruction: pull=down
endmodule
