// Logisim project Ctl_Shift_Add_Sub_Mov.circ as structural Verilog: 1 circuit, main circuit Shift_Add_Sub_Mov
module Shift_Add_Sub_Mov (
  input  [15:0] Instruction,
  input  Enable,
  output [31:0] Imm32,
  output Carry,
  output Imm32_Enable,
  output [3:0] ALU_Opcode,
  output [3:0] Flags_Update_Mask,
  output [2:0] Rm,
  output [2:0] Rn,
  output [4:0] Imm5,
  output [2:0] Rd
);

  wire and_2_out, and_3_out, and_5_out, comparator_1_eq, comparator_2_eq, condIMM5, CondiRm, or_1_out, res1;
  wire [2:0] Rd_t, resRm, ResRn;
  wire [3:0] multiplexer_14_out, multiplexer_16_out, multiplexer_17_out, multiplexer_18_out;
  wire [4:0] resIMM5;
  wire [31:0] IMM3_32, IMM8_32, IMM8_FINAL, multiplexer_11_out, negator_1_out;

  Comparator #(.width(3)) comparator_1 (.a(Instruction[13:11]), .b(3'b011), .eq(comparator_1_eq));  // open: gt, lt
  Comparator #(.width(3)) comparator_2 (.a(Instruction[13:11]), .b(3'b111), .eq(comparator_2_eq));  // open: gt, lt
  and and_1 (CondiRm, ~Instruction[13], Instruction[12], Instruction[11], ~Instruction[10]);  // AND_Gate
  Multiplexer #(.width(3)) multiplexer_1 (.in0(3'b000), .in1(Rd_t), .out(Rd), .sel(Enable));
  and and_2 (and_2_out, comparator_1_eq, Instruction[9]);
  or or_1 (or_1_out, and_2_out, comparator_2_eq);
  Multiplexer #(.width(3)) multiplexer_2 (
    .in0(Instruction[2:0]), .in1(Instruction[10:8]), .out(Rd_t), .sel(Instruction[13]));
  Multiplexer multiplexer_3 (.in0(1'b0), .in1(or_1_out), .out(Carry), .sel(Enable));
  Multiplexer #(.width(3)) multiplexer_4 (.in0(3'b000), .in1(resRm), .out(Rm), .sel(Enable));
  Multiplexer #(.width(3)) multiplexer_5 (.in0(Instruction[5:3]), .in1(Instruction[8:6]), .out(resRm), .sel(CondiRm));
  Multiplexer #(.width(3)) multiplexer_6 (
    .in0(Instruction[5:3]), .in1(Instruction[10:8]), .out(ResRn), .sel(Instruction[13]));
  Multiplexer #(.width(3)) multiplexer_7 (.in0(3'b000), .in1(ResRn), .out(Rn), .sel(Enable));
  assign IMM8_32 = {{24{1'b0}}, Instruction[7:0]};  // Bit_Extender bit_extender_1
  assign IMM3_32 = {{29{1'b0}}, Instruction[8:6]};  // Bit_Extender bit_extender_2
  Negator #(.width(32)) negator_1 (.in(IMM8_32), .out(negator_1_out));
  and and_3 (and_3_out, Instruction[13], ~Instruction[12], ~Instruction[11]);  // AND_Gate
  Multiplexer #(.width(32)) multiplexer_8 (.in0(IMM8_32), .in1(negator_1_out), .out(IMM8_FINAL), .sel(and_3_out));
  and and_4 (res1, Instruction[12], Instruction[11]);
  or or_2 (Imm32_Enable, and_5_out, Instruction[13]);
  Multiplexer #(.width(5)) multiplexer_9 (.in0({5{1'b0}}), .in1(Instruction[10:6]), .out(resIMM5), .sel(condIMM5));
  and and_5 (and_5_out, ~Instruction[13], Instruction[12], Instruction[11], Instruction[10]);  // AND_Gate
  and and_6 (condIMM5, ~Instruction[13], ~res1);  // AND_Gate
  Multiplexer #(.width(5)) multiplexer_10 (.in0({5{1'b0}}), .in1(resIMM5), .out(Imm5), .sel(Enable));
  Multiplexer #(.width(32)) multiplexer_11 (.in0({32{1'b0}}), .in1(IMM3_32), .out(multiplexer_11_out), .sel(and_5_out));
  Multiplexer #(.select(2), .width(32)) multiplexer_12 (
    .in0({32{1'b0}}), .in2(IMM8_32), .in3(IMM3_32), .out(Imm32));  // open: in1, sel
  Multiplexer #(.width(32)) multiplexer_13 (
    .in0(multiplexer_11_out), .in1(IMM8_FINAL), .out(Imm32), .sel(Instruction[13]));
  Multiplexer #(.select(3), .width(4)) multiplexer_14 (
    .in0(4'b1110), .in1(4'b1110), .in2(4'b1110), .in3(4'b1111), .in4(4'b1100), .in5(4'b1111), .in6(4'b1111),
    .in7(4'b1111), .out(multiplexer_14_out), .sel(Instruction[13:11]));
  Multiplexer #(.width(4)) multiplexer_15 (
    .in0(4'b0000), .in1(multiplexer_14_out), .out(Flags_Update_Mask), .sel(Enable));
  Multiplexer #(.width(4)) multiplexer_16 (
    .in0(4'b0101), .in1(4'b0110), .out(multiplexer_16_out), .sel(Instruction[9]));
  Multiplexer #(.select(2), .width(4)) multiplexer_17 (
    .in0(4'b0010), .in1(4'b0011), .in2(4'b0100), .in3(multiplexer_16_out), .out(multiplexer_17_out),
    .sel(Instruction[12:11]));
  Multiplexer #(.select(2), .width(4)) multiplexer_18 (
    .in0(4'b1001), .in1(4'b1010), .in2(4'b0101), .in3(4'b0110), .out(multiplexer_18_out),
    .sel(Instruction[12:11]));
  Multiplexer #(.width(4)) multiplexer_19 (
    .in0(multiplexer_17_out), .in1(multiplexer_18_out), .out(ALU_Opcode), .sel(Instruction[13]));

  // Other names for the same wires on the sheet: b11 = Instruction[11]; Opcode[2:0] = Instruction[13:11];
  //   b12 = Instruction[12]; FinalIMM5[4:0] = Imm5; FinalRn[2:0] = Rn; FLAGS[3:0] = Flags_Update_Mask;
  //   b6 = Instruction[6]; IMM3[2:0] = Instruction[8:6]; Imm5_t[4:0] = Instruction[10:6];
  //   IMM8[7:0] = Instruction[7:0]; RmAVANT[2:0] = Instruction[8:6]; b7 = Instruction[7]; b8 = Instruction[8];
  //   Rd_middle[2:0] = Instruction[10:8]; Rn_avant[2:0] = Instruction[10:8]; b9 = Instruction[9];
  //   b10 = Instruction[10]; b0 = Instruction[0]; Rd_last[2:0] = Instruction[2:0]; b1 = Instruction[1];
  //   b2 = Instruction[2]; b3 = Instruction[3]; RmAPRES[2:0] = Instruction[5:3]; Rn_apres[2:0] = Instruction[5:3];
  //   b4 = Instruction[4]; b5 = Instruction[5]; b14 = Instruction[14]; b15 = Instruction[15]; b13 = Instruction[13];
  //   RdFINAL[2:0] = Rd; RmFinal[2:0] = Rm

  // Notes on the sheet:
  //   Pull output low on Enable = 0
  //   only ADD and SUB use Rm
endmodule
