// Logisim project Ctl_Shift_Add_Sub_Mov.circ.circ as structural Verilog: 1 circuit, main circuit Shift_Add_Sub_Mov
module Shift_Add_Sub_Mov (
  input  Enable,
  input  [15:0] Instruction,
  output [3:0] Flags_Update_Mask,
  output Carry,
  output [2:0] Rm,
  output [2:0] Rn,
  output [2:0] Rd,
  output [4:0] Imm5,
  output [31:0] Imm32,
  output [3:0] ALU_Opcode,
  output Imm32_Enable
);

  wire and_1_out, and_3_out, and_5_out, and_8_out, and_9_out, condIMM5, CondiRm, or_2_out, or_3_out, res1;
  wire [2:0] Rd_t, resRm, ResRn;
  wire [3:0] multiplexer_13_out, multiplexer_14_out, multiplexer_15_out;
  wire [4:0] resIMM5;
  wire [31:0] IMM3_32, IMM8_32, IMM8_FINAL, multiplexer_3_out, negator_1_out;

  or or_1 (Imm32_Enable, and_1_out, Instruction[13]);
  Multiplexer #(.width(3)) multiplexer_1 (
    .in0(Instruction[5:3]), .in1(Instruction[10:8]), .out(ResRn), .sel(Instruction[13]));
  Multiplexer #(.select(2), .width(32)) multiplexer_2 (
    .in0({32{1'b0}}), .in2(IMM8_32), .in3(IMM3_32), .out(Imm32));  // open: in1, sel
  and and_1 (and_1_out, ~Instruction[13], Instruction[12], Instruction[11], Instruction[10]);  // AND_Gate
  Multiplexer #(.width(32)) multiplexer_3 (.in0({32{1'b0}}), .in1(IMM3_32), .out(multiplexer_3_out), .sel(and_1_out));
  Multiplexer #(.width(3)) multiplexer_4 (
    .in0(Instruction[2:0]), .in1(Instruction[10:8]), .out(Rd_t), .sel(Instruction[13]));
  Multiplexer #(.width(32)) multiplexer_5 (
    .in0(multiplexer_3_out), .in1(IMM8_FINAL), .out(Imm32), .sel(Instruction[13]));
  Multiplexer #(.width(3)) multiplexer_6 (.in0(3'b000), .in1(ResRn), .out(Rn), .sel(Enable));
  and and_2 (condIMM5, ~Instruction[13], ~res1);  // AND_Gate
  Multiplexer #(.width(5)) multiplexer_7 (.in0({5{1'b0}}), .in1(resIMM5), .out(Imm5), .sel(Enable));
  Multiplexer #(.width(5)) multiplexer_8 (.in0({5{1'b0}}), .in1(Instruction[10:6]), .out(resIMM5), .sel(condIMM5));
  and and_3 (and_3_out, Instruction[11], Instruction[12]);
  or or_2 (or_2_out, Instruction[9], Instruction[13]);
  Negator #(.width(32)) negator_1 (.in(IMM8_32), .out(negator_1_out));
  and and_4 (Carry, and_3_out, or_2_out);
  Multiplexer #(.width(3)) multiplexer_9 (.in0(3'b000), .in1(Rd_t), .out(Rd), .sel(Enable));
  Multiplexer #(.width(32)) multiplexer_10 (.in0(IMM8_32), .in1(negator_1_out), .out(IMM8_FINAL), .sel(and_5_out));
  and and_5 (and_5_out, Instruction[13], ~Instruction[12], ~Instruction[11]);  // AND_Gate
  assign IMM8_32 = {{24{1'b0}}, Instruction[7:0]};  // Bit_Extender bit_extender_1
  assign IMM3_32 = {{29{1'b0}}, Instruction[8:6]};  // Bit_Extender bit_extender_2
  and and_6 (res1, Instruction[12], Instruction[11]);
  and and_7 (CondiRm, ~Instruction[13], Instruction[12], Instruction[11], ~Instruction[10]);  // AND_Gate
  Multiplexer #(.width(3)) multiplexer_11 (.in0(3'b000), .in1(resRm), .out(Rm), .sel(Enable));
  Multiplexer #(.width(3)) multiplexer_12 (.in0(Instruction[5:3]), .in1(Instruction[8:6]), .out(resRm), .sel(CondiRm));
  Multiplexer #(.width(4)) multiplexer_13 (
    .in0(4'b0101), .in1(4'b0110), .out(multiplexer_13_out), .sel(Instruction[9]));
  and and_8 (and_8_out, ~Instruction[13], ~Instruction[12]);  // AND_Gate
  Multiplexer #(.select(2), .width(4)) multiplexer_14 (
    .in0(4'b0010), .in1(4'b0011), .in2(4'b0100), .in3(multiplexer_13_out), .out(multiplexer_14_out),
    .sel(Instruction[12:11]));
  Multiplexer #(.select(2), .width(4)) multiplexer_15 (
    .in0(4'b1001), .in1(4'b1010), .in2(4'b0101), .in3(4'b0110), .out(multiplexer_15_out),
    .sel(Instruction[12:11]));
  or or_3 (or_3_out, and_8_out, ~Flags_Update_Mask[1]);  // OR_Gate
  not not_1 (Flags_Update_Mask[0], or_3_out);
  Multiplexer #(.width(4)) multiplexer_16 (
    .in0(multiplexer_14_out), .in1(multiplexer_15_out), .out(ALU_Opcode), .sel(Instruction[13]));
  and and_9 (and_9_out, Instruction[13], ~Instruction[12], ~Instruction[11]);  // AND_Gate
  not not_2 (Flags_Update_Mask[1], and_9_out);

  assign Flags_Update_Mask[3:2] = 2'b11;

  // Other names for the same wires on the sheet: b11 = Instruction[11]; b12 = Instruction[12]; FinalIMM5[4:0] = Imm5;
  //   FinalRn[2:0] = Rn; FLAGS[1:0] = Flags_Update_Mask[1:0]; V = Flags_Update_Mask[0]; C = Flags_Update_Mask[1];
  //   b6 = Instruction[6]; IMM3[2:0] = Instruction[8:6]; Imm5_t[4:0] = Instruction[10:6];
  //   IMM8[7:0] = Instruction[7:0]; RmAVANT[2:0] = Instruction[8:6]; b7 = Instruction[7]; b8 = Instruction[8];
  //   Rd_middle[2:0] = Instruction[10:8]; Rn_avant[2:0] = Instruction[10:8]; b9 = Instruction[9];
  //   b10 = Instruction[10]; b0 = Instruction[0]; Rd_last[2:0] = Instruction[2:0]; b1 = Instruction[1];
  //   b2 = Instruction[2]; b3 = Instruction[3]; RmAPRES[2:0] = Instruction[5:3]; Rn_apres[2:0] = Instruction[5:3];
  //   b4 = Instruction[4]; b5 = Instruction[5]; b13 = Instruction[13]; b14 = Instruction[14]; b15 = Instruction[15];
  //   RdFINAL[2:0] = Rd; RmFinal[2:0] = Rm

  // Notes on the sheet:
  //   Pull output low on Enable = 0
  //   Enable carry for SUB since it is reversed in ALU
  //   ALU will use Imm32 instead of Rm
  //   only ADD and SUB use Rm
  //   Note 3: Imm32_Enable forces the use of the immediate for Rm register
  //   Note: ALU uses Rn register for shifts. Use Rn instead of Rm for shifts (immediate) here too
  //   Note 2: MOV uses RSB ALU opcode with Imm8 reversed so that it is copied to output register
endmodule
